# Fritzing sketch Fritzing sketch (saved by Fritzing 0.9.3b)
breadboards: 1

parts:
  LED1 = LED - 5mm [color="Green (570nm)" package="5 mm [THT]"]
  S1 = Pushbutton [package="[THT]"]
  U2 = NodeMCU V3.0

nets:
  N1: LED1.cathode, U2.D1
  N2: LED1.anode, S1.Pin_1, S1.Pin_2, U2.GND#6, U2.GND#13, U2.GND#16, U2.GND#33
  N3: S1.Pin_3, S1.Pin_4, U2.D2

custom parts:
  NodeMCU V3.0: ESP8266 based NodeMCU
